// Digital circuit CPU 8.dig as structural Verilog
module CPU_8 (
  input  [7:0] DAT,
  input  [7:0] ADDlo,
  input  [7:0] ADDhi,
  input  Clock,
  input  pcd,
  input  nRST,
  input  nNMI,
  input  nIRJ,
  input  nIRK,
  input  nDMA,
  input  nWAIT,
  input  nHALT,
  output CLK1,
  output CLK2
);

  wire A_clr, add_1_c_o, alu_1_p13, alu_1_p14, and_1_out, and_2_out, and_3_out, and_4_out, and_5_out,
       and_6_out, and_7_out, and_8_out, and_9_out, and_10_out, and_11_out, and_12_out, BCD_clr, BRK_Vout,
       comparator_1_eq, COND_C, COND_N, COND_P, COND_RES, COND_X, COND_Y, COND_Z, CONV_V, D0, D1, D2, D3, D4,
       D5, D6, D7, demultiplexer_1_out_0, demultiplexer_1_out_1, demultiplexer_1_out_2,
       demultiplexer_1_out_3, demultiplexer_1_out_4, demultiplexer_1_out_5, demultiplexer_1_out_6,
       demultiplexer_1_out_7, demultiplexer_2_out_0, demultiplexer_2_out_1, demultiplexer_3_out_1,
       demultiplexer_3_out_2, demultiplexer_3_out_3, demultiplexer_4_out_0, demultiplexer_4_out_1,
       demultiplexer_4_out_2, demultiplexer_4_out_3, demultiplexer_4_out_4, demultiplexer_4_out_5,
       demultiplexer_4_out_6, demultiplexer_4_out_7, demultiplexer_5_out_0, demultiplexer_5_out_1,
       demultiplexer_5_out_2, demultiplexer_5_out_3, demultiplexer_5_out_4, demultiplexer_5_out_5,
       demultiplexer_5_out_6, demultiplexer_5_out_7, demultiplexer_6_out_0, demultiplexer_6_out_1,
       demultiplexer_6_out_2, demultiplexer_6_out_3, demultiplexer_6_out_4, demultiplexer_6_out_5,
       demultiplexer_7_out_1, demultiplexer_7_out_2, demultiplexer_7_out_3, demultiplexer_7_out_4,
       demultiplexer_7_out_5, demultiplexer_7_out_6, demultiplexer_8_out_0, demultiplexer_8_out_1,
       demultiplexer_8_out_2, demultiplexer_8_out_3, demultiplexer_8_out_4, demultiplexer_8_out_5,
       demultiplexer_8_out_6, demultiplexer_8_out_7, demultiplexer_9_out_0, demultiplexer_9_out_1,
       demultiplexer_9_out_2, demultiplexer_9_out_3, demultiplexer_9_out_4, demultiplexer_9_out_5,
       demultiplexer_9_out_6, demultiplexer_9_out_7, demultiplexer_10_out_0, demultiplexer_10_out_1,
       demultiplexer_10_out_2, demultiplexer_10_out_3, demultiplexer_10_out_4, demultiplexer_10_out_5,
       demultiplexer_10_out_6, demultiplexer_11_out_1, demultiplexer_11_out_2, demultiplexer_11_out_3,
       demultiplexer_11_out_4, demultiplexer_11_out_5, demultiplexer_11_out_6, demultiplexer_11_out_7,
       DMA_ack, driverinvsel_1_out, driverinvsel_2_out, driverinvsel_3_out, FLAG_C, FLAG_V, IRJ_clr,
       IRJ_FTdat, IRJ_Vout, IRK_clr, IRK_FTdat, IRK_Vout, IRQ_en, IX_clr, IY_clr, memory_map_state_1_q0,
       memory_map_state_1_q1, memory_map_state_1_q3, memory_map_state_1_q4, nA_DATout, nA_st, nADD_ADSout,
       nB_DATout, nB_st, nBC_ADSout, nBIT_DATout, nBYTE_DATout, nC_DATout, nC_Fst, nC_st, nD_DATout, nD_st,
       nF_ALUin, nF_DATin, nF_DATout, nIR_st, nIX_ADSout, nIXH_DATout, nIXH_st, nIXL_DATout, nIXL_st,
       nIY_ADSout, nIYH_DATout, nIYH_st, nIYL_DATout, nIYL_st, nJ_Fst, nK_Fst, nMAR_ADSout, nMARH_st,
       nMARL_st, nMDR_DATout, nMDR_st, nMEM_DATout, nMEM_en, nMEM_in, NMI_Vout, nNZ_Fst, nor_1_out,
       nor_2_out, not_1_out, not_2_out, not_3_out, not_4_out, not_5_out, not_6_out, not_11_out, not_12_out,
       not_13_out, not_14_out, not_15_out, not_16_out, not_17_out, not_18_out, not_19_out, not_20_out,
       not_57_out, not_58_out, not_59_out, not_61_out, not_62_out, not_63_out, not_64_out, not_65_out,
       not_66_out, not_82_out, not_83_out, not_84_out, nPC_ADSout, nPCH_DATout, nPCH_st, nPCL_DATout,
       nPCL_st, nREG_ADDin, nREG_DATin, nREL_st, nSEQ_en, nSEQ_st, nSP_ADSout, nSP_DATout, nSP_st,
       nSUM_DATout, nSUM_st, nTADD_st, nTMEM_st, nV_Fst, nX_Fst, nY_Fst, or_1_out, or_2_out, or_3_out,
       or_4_out, or_5_out, or_6_out, or_7_out, or_8_out, or_9_out, or_16_out, or_23_out, or_24_out,
       or_25_out, PC_en, PCL_ovf, RST_Vout, SEQ_val, SP_dir, SP_en, t_ff_1_nq, t_ff_1_q, TEMP_clr, X_FTdat,
       Y_FTdat, \Σ_Csel , \Σ_Cval , \Σ_M , \Σ_rot ;
  wire [1:0] alu_1_p11, d_ff_1_q, FLAG_NZ, MD_q;
  wire [2:0] A_sel, C_sel, Z_sel;
  wire [3:0] \Σ_sel ;
  wire [4:0] F_sel, \µSEQ_out ;
  wire [5:0] B_sel, R_sel;
  wire [7:0] A_out, add_1_s, add_2_s, ADDH_out, ADDL_out, ADDRESS_HIin, ADDRESS_HIout, ADDRESS_LOin,
       ADDRESS_LOout, alu_1_p1, B_out, bitextender_1_out, bitextender_2_out, C_out, D_out, DATA_out,
       driverinvsel_21_out, driverinvsel_22_out, driverinvsel_23_out, driverinvsel_24_out,
       driverinvsel_34_out, driverinvsel_35_out, driverinvsel_36_out, driverinvsel_37_out,
       driverinvsel_46_out, driverinvsel_47_out, driverinvsel_48_out, driverinvsel_49_out, IR_q, IXH_out,
       IXL_out, IYH_out, IYL_out, MARH_out, MARL_out, MDR_q, or_13_out, or_14_out, or_15_out, or_17_out,
       or_18_out, or_19_out, or_20_out, or_21_out, or_22_out, PCH_out, PCL_out, ramsingleportsel_1_d,
       REL_out, rom_1_d, SP_out, TMEM_out, TSR_q;
  wire [11:5] DMA_q;
  wire [47:0] \µCODE_d ;
  wire [47:36] CTRL_q;

  CounterPreset IRJ (
    .en(~1'b1), .C(CLK2), .dir(1'b0), .in(D6), .ld(~nJ_Fst), .clr(IRJ_clr), .out(IRJ_FTdat));  // open: ovf
  CounterPreset IRK (
    .en(~1'b1), .C(CLK2), .dir(1'b0), .in(D7), .ld(~nK_Fst), .clr(IRK_clr), .out(IRK_FTdat));  // open: ovf
  and and_1 (and_1_out, ~COND_N, FLAG_NZ[0]);  // And
  and and_2 (and_2_out, ~COND_Z, FLAG_NZ[1]);  // And
  and and_3 (and_3_out, ~CONV_V, FLAG_V);  // And
  Comparator #(.Bits(16)) comparator_1 (
    .a({ADDRESS_HIin, ADDRESS_LOin}), .b({16{1'b0}}), .eq(comparator_1_eq));  // open: gt, lt
  Register #(.Bits(2)) MD (.D({D1, D0}), .C(CLK2), .en(~memory_map_state_1_q3), .Q(MD_q));
  Register #(.Bits(8)) IO (.D({D7, D6, D5, D4, D3, D2, D1, D0}), .C(CLK2), .en(~memory_map_state_1_q4));  // open: Q
  or or_1 (or_1_out, and_1_out, and_2_out);
  and and_4 (and_4_out, ~COND_C, ~FLAG_C);  // And
  assign driverinvsel_1_out = ~nF_ALUin ? comparator_1_eq : 1'bz;  // DriverInvSel driverinvsel_1
  D_FF #(.Bits(2)) d_ff_1 (.D(MD_q), .C(CLK1), .Q(d_ff_1_q));  // open: nQ
  nor nor_1 (nor_1_out, nIRJ, IRJ_FTdat);
  nor nor_2 (nor_2_out, nIRK, IRK_FTdat);
  and and_5 (and_5_out, ~COND_X, X_FTdat);  // And
  assign driverinvsel_2_out = ~nF_DATin ? D5 : 1'bz;  // DriverInvSel driverinvsel_2
  assign driverinvsel_3_out = ~nF_DATin ? D4 : 1'bz;  // DriverInvSel driverinvsel_3
  not not_1 (not_1_out, nDMA);
  not not_2 (not_2_out, nRST);
  not not_3 (not_3_out, nNMI);
  not not_4 (not_4_out, nHALT);
  or or_2 (or_2_out, and_3_out, and_4_out);
  and and_6 (and_6_out, ~COND_Y, Y_FTdat);  // And
  and and_7 (and_7_out, not_1_out, IRQ_en);
  and and_8 (and_8_out, not_2_out, IRQ_en);
  and and_9 (and_9_out, not_3_out, IRQ_en);
  and and_10 (and_10_out, nor_1_out, IRQ_en);
  and and_11 (and_11_out, nor_2_out, IRQ_en);
  and and_12 (and_12_out, not_4_out, IRQ_en);
  or or_3 (or_3_out, and_5_out, and_6_out);
  or or_4 (or_4_out, driverinvsel_1_out, driverinvsel_2_out);
  PullDown pulldown_1 (.out(driverinvsel_2_out));
  or or_5 (or_5_out, driverinvsel_1_out, driverinvsel_3_out);
  PullDown pulldown_2 (.out(driverinvsel_3_out));
  PullDown pulldown_3 (.out(driverinvsel_1_out));
  MEMORY_MAP_STATE memory_map_state_1 (
    .A({ADDRESS_HIin, ADDRESS_LOin}), .WR(nMEM_in), .MD(d_ff_1_q), .EN(nMEM_en), .Q4(memory_map_state_1_q4),
    .Q3(memory_map_state_1_q3), .Q1(memory_map_state_1_q1), .Q0(memory_map_state_1_q0));  // open: Q2
  or or_6 (or_6_out, or_2_out, or_3_out);
  CounterPreset #(.Bits(5)) \u_µSEQ  (
    .en(~nSEQ_en), .C(CLK2), .dir(1'b0), .in({4'b0000, SEQ_val}), .ld(~nSEQ_st), .clr(1'b0), .out(\µSEQ_out ));  // open: ovf
  D_FF DMA (.D(and_7_out), .C(CLK2), .Q(DMA_q[5]));  // open: nQ
  D_FF RESET (.D(and_8_out), .C(CLK2), .Q(DMA_q[6]));  // open: nQ
  D_FF NMI (.D(and_9_out), .C(CLK2), .Q(DMA_q[7]));  // open: nQ
  D_FF IRJ_2 (.D(and_10_out), .C(CLK2), .Q(DMA_q[8]));  // open: nQ
  D_FF IRK_2 (.D(and_11_out), .C(CLK2), .Q(DMA_q[9]));  // open: nQ
  D_FF HALT (.D(and_12_out), .C(CLK2), .Q(DMA_q[10]));  // open: nQ
  D_FF COND (.D(COND_RES), .C(CLK2), .Q(DMA_q[11]));  // open: nQ
  Register #(.Bits(8)) IR (.D({D7, D6, D5, D4, D3, D2, D1, D0}), .C(CLK2), .en(~nIR_st), .Q(IR_q));
  Register Y_F (.D(or_4_out), .C(CLK2), .en(~nY_Fst), .Q(Y_FTdat));
  Register X_F (.D(or_5_out), .C(CLK2), .en(~nX_Fst), .Q(X_FTdat));
  or or_7 (or_7_out, or_1_out, or_6_out);
  not not_5 (not_5_out, or_7_out);
  assign COND_RES = ~COND_P ? or_7_out : 1'bz;  // DriverInvSel driverinvsel_4
  RAMSinglePortSel #(.AddrBits(16), .Bits(8)) ramsingleportsel_1 (
    .A({ADDRESS_HIin, ADDRESS_LOin}), .CS(~memory_map_state_1_q0), .WE(~nMEM_in), .OE(~nMEM_DATout),
    .D(ramsingleportsel_1_d));
  ROM #(.AddrBits(16), .Bits(8)) rom_1 (.A({ADDRESS_HIin, ADDRESS_LOin}), .sel(not_6_out), .D(rom_1_d));
  not not_6 (not_6_out, memory_map_state_1_q1);
  assign COND_RES = ~COND_N ? not_5_out : 1'bz;  // DriverInvSel driverinvsel_5
  ROM #(.AddrBits(20), .Bits(48)) \u_µCODE  (.A({IR_q, DMA_q, \µSEQ_out }), .sel(1'b1), .D(\µCODE_d ));
  or or_8 (or_8_out, nMEM_DATout, memory_map_state_1_q0);
  or or_9 (or_9_out, nMEM_DATout, memory_map_state_1_q1);
  PullDown #(.Bits(8)) pulldown_4 (.out(ramsingleportsel_1_d));
  PullDown #(.Bits(8)) pulldown_5 (.out(rom_1_d));
  D_FF #(.Bits(48)) CTRL (
    .D(\µCODE_d ), .C(CLK1),
    .Q({CTRL_q[47:45], DMA_ack, IRQ_en, SEQ_val, CTRL_q[41:40], nF_ALUin, nREG_DATin, CTRL_q[37:36], SP_dir, COND_P, \Σ_rot , \Σ_Cval , \Σ_Csel , \Σ_M , \Σ_sel , Z_sel, F_sel, C_sel, A_sel, B_sel, R_sel}));  // open: nQ
  Demultiplexer #(.Selector_Bits(3)) demultiplexer_1 (
    .sel(F_sel[2:0]), .in(F_sel[3]), .out_0(demultiplexer_1_out_0), .out_1(demultiplexer_1_out_1),
    .out_2(demultiplexer_1_out_2), .out_3(demultiplexer_1_out_3), .out_4(demultiplexer_1_out_4),
    .out_5(demultiplexer_1_out_5), .out_6(demultiplexer_1_out_6), .out_7(demultiplexer_1_out_7));
  Demultiplexer #(.Selector_Bits(3)) demultiplexer_2 (
    .sel(F_sel[2:0]), .in(F_sel[4]), .out_0(demultiplexer_2_out_0), .out_1(demultiplexer_2_out_1));  // open: out_2, out_3, out_4, out_5, out_6, out_7
  Demultiplexer #(.Selector_Bits(3)) demultiplexer_3 (
    .sel(Z_sel), .in(1'b1), .out_1(demultiplexer_3_out_1), .out_2(demultiplexer_3_out_2),
    .out_3(demultiplexer_3_out_3), .out_4(BCD_clr), .out_5(IRK_clr), .out_6(IRJ_clr), .out_7(TEMP_clr));  // open: out_0
  assign ramsingleportsel_1_d = ~nMEM_in ? TMEM_out : 8'bz;  // DriverInvSel driverinvsel_6
  assign DATA_out = ~or_8_out ? ramsingleportsel_1_d : 8'bz;  // DriverInvSel driverinvsel_7
  assign DATA_out = ~or_9_out ? rom_1_d : 8'bz;  // DriverInvSel driverinvsel_8
  not not_7 (SP_en, CTRL_q[36]);
  not not_8 (PC_en, CTRL_q[37]);
  not not_9 (nSEQ_en, CTRL_q[40]);
  not not_10 (nSEQ_st, CTRL_q[41]);
  not not_11 (not_11_out, demultiplexer_1_out_0);
  not not_12 (not_12_out, demultiplexer_1_out_1);
  not not_13 (not_13_out, demultiplexer_1_out_2);
  not not_14 (not_14_out, demultiplexer_1_out_3);
  not not_15 (not_15_out, demultiplexer_1_out_4);
  not not_16 (not_16_out, demultiplexer_1_out_5);
  not not_17 (not_17_out, demultiplexer_1_out_6);
  not not_18 (not_18_out, demultiplexer_1_out_7);
  not not_19 (not_19_out, demultiplexer_2_out_0);
  not not_20 (not_20_out, demultiplexer_2_out_1);
  CounterPreset #(.Bits(8)) TMEM (
    .en(~1'b1), .C(CLK2), .dir(1'b0), .in({D7, D6, D5, D4, D3, D2, D1, D0}), .ld(~nTMEM_st), .clr(TEMP_clr),
    .out(TMEM_out));  // open: ovf
  PullDown #(.Bits(8)) pulldown_6 (.out(DATA_out));
  not not_21 (COND_N, COND_P);
  not not_22 (nREG_ADDin, nREG_DATin);
  not not_23 (nF_DATin, nF_ALUin);
  or or_10 (A_clr, demultiplexer_3_out_1, BCD_clr);
  or or_11 (IX_clr, demultiplexer_3_out_2, BCD_clr);
  or or_12 (IY_clr, demultiplexer_3_out_3, BCD_clr);
  and and_13 (nNZ_Fst, not_11_out, not_17_out, not_14_out);
  and and_14 (nV_Fst, not_14_out, not_17_out, not_12_out);
  and and_15 (nC_Fst, not_14_out, not_17_out, not_13_out);
  and and_16 (nX_Fst, not_15_out, not_17_out);
  and and_17 (nY_Fst, not_16_out, not_17_out);
  and and_18 (nJ_Fst, not_18_out, not_20_out);
  and and_19 (nK_Fst, not_19_out, not_20_out);
  Demultiplexer #(.Selector_Bits(3)) demultiplexer_4 (
    .sel(B_sel[2:0]), .in(B_sel[3]), .out_0(demultiplexer_4_out_0), .out_1(demultiplexer_4_out_1),
    .out_2(demultiplexer_4_out_2), .out_3(demultiplexer_4_out_3), .out_4(demultiplexer_4_out_4),
    .out_5(demultiplexer_4_out_5), .out_6(demultiplexer_4_out_6), .out_7(demultiplexer_4_out_7));
  not not_24 (nA_DATout, demultiplexer_4_out_0);
  not not_25 (nB_DATout, demultiplexer_4_out_1);
  not not_26 (nC_DATout, demultiplexer_4_out_2);
  not not_27 (nD_DATout, demultiplexer_4_out_3);
  not not_28 (nF_DATout, demultiplexer_4_out_4);
  not not_29 (nPCH_DATout, demultiplexer_4_out_5);
  not not_30 (nPCL_DATout, demultiplexer_4_out_6);
  not not_31 (nSP_DATout, demultiplexer_4_out_7);
  not not_32 (nIXH_DATout, demultiplexer_5_out_0);
  Demultiplexer #(.Selector_Bits(3)) demultiplexer_5 (
    .sel(B_sel[2:0]), .in(B_sel[4]), .out_0(demultiplexer_5_out_0), .out_1(demultiplexer_5_out_1),
    .out_2(demultiplexer_5_out_2), .out_3(demultiplexer_5_out_3), .out_4(demultiplexer_5_out_4),
    .out_5(demultiplexer_5_out_5), .out_6(demultiplexer_5_out_6), .out_7(demultiplexer_5_out_7));
  not not_33 (nIXL_DATout, demultiplexer_5_out_1);
  not not_34 (nIYH_DATout, demultiplexer_5_out_2);
  not not_35 (nIYL_DATout, demultiplexer_5_out_3);
  not not_36 (nSUM_DATout, demultiplexer_5_out_4);
  not not_37 (nMEM_DATout, demultiplexer_5_out_5);
  not not_38 (nBYTE_DATout, demultiplexer_5_out_6);
  not not_39 (RST_Vout, demultiplexer_5_out_7);
  not not_40 (NMI_Vout, demultiplexer_6_out_0);
  Demultiplexer #(.Selector_Bits(3)) demultiplexer_6 (
    .sel(B_sel[2:0]), .in(B_sel[5]), .out_0(demultiplexer_6_out_0), .out_1(demultiplexer_6_out_1),
    .out_2(demultiplexer_6_out_2), .out_3(demultiplexer_6_out_3), .out_4(demultiplexer_6_out_4),
    .out_5(demultiplexer_6_out_5));  // open: out_6, out_7
  not not_41 (BRK_Vout, demultiplexer_6_out_1);
  not not_42 (IRJ_Vout, demultiplexer_6_out_2);
  not not_43 (IRK_Vout, demultiplexer_6_out_3);
  not not_44 (nBIT_DATout, demultiplexer_6_out_4);
  not not_45 (nMDR_DATout, demultiplexer_6_out_5);
  Demultiplexer #(.Selector_Bits(3)) demultiplexer_7 (
    .sel(C_sel), .in(1'b1), .out_1(demultiplexer_7_out_1), .out_2(demultiplexer_7_out_2),
    .out_3(demultiplexer_7_out_3), .out_4(demultiplexer_7_out_4), .out_5(demultiplexer_7_out_5),
    .out_6(demultiplexer_7_out_6));  // open: out_0, out_7
  not not_46 (COND_N, demultiplexer_7_out_1);
  not not_47 (COND_Z, demultiplexer_7_out_2);
  not not_48 (CONV_V, demultiplexer_7_out_3);
  not not_49 (COND_C, demultiplexer_7_out_4);
  not not_50 (COND_X, demultiplexer_7_out_5);
  not not_51 (COND_Y, demultiplexer_7_out_6);
  PullDown #(.Bits(8)) pulldown_7 (.out(ADDRESS_LOout));
  PullDown #(.Bits(8)) pulldown_8 (.out(ADDlo));
  PullDown #(.Bits(8)) pulldown_9 (.out(ADDRESS_HIout));
  PullDown #(.Bits(8)) pulldown_10 (.out(ADDhi));
  PullDown #(.Bits(8)) pulldown_11 (.out(DATA_out));
  PullDown #(.Bits(8)) pulldown_12 (.out(DAT));
  assign or_13_out = ADDRESS_LOout | ADDlo;  // Or or_13, 8 bits wide
  assign or_14_out = ADDRESS_HIout | ADDhi;  // Or or_14, 8 bits wide
  assign or_15_out = DATA_out | DAT;  // Or or_15, 8 bits wide
  DiodeForward diodeforward_1 (.in(or_13_out[0]), .out(ADDRESS_LOin[0]));
  DiodeForward diodeforward_2 (.in(or_13_out[1]), .out(ADDRESS_LOin[1]));
  DiodeForward diodeforward_3 (.in(or_13_out[2]), .out(ADDRESS_LOin[2]));
  DiodeForward diodeforward_4 (.in(or_13_out[3]), .out(ADDRESS_LOin[3]));
  DiodeForward diodeforward_5 (.in(or_13_out[4]), .out(ADDRESS_LOin[4]));
  DiodeForward diodeforward_6 (.in(or_13_out[5]), .out(ADDRESS_LOin[5]));
  DiodeForward diodeforward_7 (.in(or_13_out[6]), .out(ADDRESS_LOin[6]));
  DiodeForward diodeforward_8 (.in(or_13_out[7]), .out(ADDRESS_LOin[7]));
  DiodeForward diodeforward_9 (.in(or_14_out[0]), .out(ADDRESS_HIin[0]));
  DiodeForward diodeforward_10 (.in(or_14_out[1]), .out(ADDRESS_HIin[1]));
  DiodeForward diodeforward_11 (.in(or_14_out[2]), .out(ADDRESS_HIin[2]));
  DiodeForward diodeforward_12 (.in(or_14_out[3]), .out(ADDRESS_HIin[3]));
  DiodeForward diodeforward_13 (.in(or_14_out[4]), .out(ADDRESS_HIin[4]));
  DiodeForward diodeforward_14 (.in(or_14_out[5]), .out(ADDRESS_HIin[5]));
  DiodeForward diodeforward_15 (.in(or_14_out[6]), .out(ADDRESS_HIin[6]));
  DiodeForward diodeforward_16 (.in(or_14_out[7]), .out(ADDRESS_HIin[7]));
  PullDown pulldown_13 (.out(ADDRESS_HIin[7]));
  PullDown pulldown_14 (.out(ADDRESS_HIin[6]));
  Demultiplexer #(.Selector_Bits(3)) demultiplexer_8 (
    .sel(R_sel[2:0]), .in(R_sel[3]), .out_0(demultiplexer_8_out_0), .out_1(demultiplexer_8_out_1),
    .out_2(demultiplexer_8_out_2), .out_3(demultiplexer_8_out_3), .out_4(demultiplexer_8_out_4),
    .out_5(demultiplexer_8_out_5), .out_6(demultiplexer_8_out_6), .out_7(demultiplexer_8_out_7));
  Demultiplexer #(.Selector_Bits(3)) demultiplexer_9 (
    .sel(R_sel[2:0]), .in(R_sel[4]), .out_0(demultiplexer_9_out_0), .out_1(demultiplexer_9_out_1),
    .out_2(demultiplexer_9_out_2), .out_3(demultiplexer_9_out_3), .out_4(demultiplexer_9_out_4),
    .out_5(demultiplexer_9_out_5), .out_6(demultiplexer_9_out_6), .out_7(demultiplexer_9_out_7));
  Demultiplexer #(.Selector_Bits(3)) demultiplexer_10 (
    .sel(R_sel[2:0]), .in(R_sel[5]), .out_0(demultiplexer_10_out_0), .out_1(demultiplexer_10_out_1),
    .out_2(demultiplexer_10_out_2), .out_3(demultiplexer_10_out_3), .out_4(demultiplexer_10_out_4),
    .out_5(demultiplexer_10_out_5), .out_6(demultiplexer_10_out_6));  // open: out_7
  Demultiplexer #(.Selector_Bits(3)) demultiplexer_11 (
    .sel(A_sel), .in(1'b1), .out_1(demultiplexer_11_out_1), .out_2(demultiplexer_11_out_2),
    .out_3(demultiplexer_11_out_3), .out_4(demultiplexer_11_out_4), .out_5(demultiplexer_11_out_5),
    .out_6(demultiplexer_11_out_6), .out_7(demultiplexer_11_out_7));  // open: out_0
  PullDown pulldown_15 (.out(ADDRESS_HIin[5]));
  PullDown pulldown_16 (.out(ADDRESS_HIin[4]));
  PullDown pulldown_17 (.out(ADDRESS_HIin[3]));
  PullDown pulldown_18 (.out(ADDRESS_HIin[2]));
  not not_52 (nA_st, demultiplexer_8_out_0);
  not not_53 (nB_st, demultiplexer_8_out_1);
  not not_54 (nC_st, demultiplexer_8_out_2);
  not not_55 (nD_st, demultiplexer_8_out_3);
  not not_56 (nIR_st, demultiplexer_8_out_4);
  not not_57 (not_57_out, demultiplexer_8_out_5);
  not not_58 (not_58_out, demultiplexer_8_out_6);
  not not_59 (not_59_out, demultiplexer_8_out_7);
  not not_60 (nSP_st, demultiplexer_9_out_0);
  not not_61 (not_61_out, demultiplexer_9_out_1);
  not not_62 (not_62_out, demultiplexer_9_out_2);
  not not_63 (not_63_out, demultiplexer_9_out_3);
  not not_64 (not_64_out, demultiplexer_9_out_4);
  not not_65 (not_65_out, demultiplexer_9_out_5);
  not not_66 (not_66_out, demultiplexer_9_out_6);
  not not_67 (nREL_st, demultiplexer_9_out_7);
  not not_68 (nMARH_st, demultiplexer_10_out_0);
  not not_69 (nMARL_st, demultiplexer_10_out_1);
  not not_70 (nSUM_st, demultiplexer_10_out_2);
  not not_71 (nMEM_in, demultiplexer_10_out_3);
  not not_72 (nTMEM_st, demultiplexer_10_out_4);
  not not_73 (nTADD_st, demultiplexer_10_out_5);
  not not_74 (nMDR_st, demultiplexer_10_out_6);
  not not_75 (nBC_ADSout, demultiplexer_11_out_1);
  not not_76 (nPC_ADSout, demultiplexer_11_out_2);
  not not_77 (nSP_ADSout, demultiplexer_11_out_3);
  not not_78 (nIX_ADSout, demultiplexer_11_out_4);
  not not_79 (nIY_ADSout, demultiplexer_11_out_5);
  not not_80 (nMAR_ADSout, demultiplexer_11_out_6);
  not not_81 (nADD_ADSout, demultiplexer_11_out_7);
  PullDown pulldown_19 (.out(ADDRESS_LOin[7]));
  PullDown pulldown_20 (.out(ADDRESS_LOin[6]));
  PullDown pulldown_21 (.out(ADDRESS_HIin[1]));
  PullDown pulldown_22 (.out(ADDRESS_HIin[0]));
  DiodeForward diodeforward_17 (.in(or_15_out[0]), .out(D0));
  DiodeForward diodeforward_18 (.in(or_15_out[1]), .out(D1));
  DiodeForward diodeforward_19 (.in(or_15_out[2]), .out(D2));
  DiodeForward diodeforward_20 (.in(or_15_out[3]), .out(D3));
  DiodeForward diodeforward_21 (.in(or_15_out[4]), .out(D4));
  DiodeForward diodeforward_22 (.in(or_15_out[5]), .out(D5));
  DiodeForward diodeforward_23 (.in(or_15_out[6]), .out(D6));
  DiodeForward diodeforward_24 (.in(or_15_out[7]), .out(D7));
  PullDown pulldown_23 (.out(D7));
  PullDown pulldown_24 (.out(D6));
  assign DATA_out = ~nBYTE_DATout ? {8{1'b1}} : 8'bz;  // DriverInvSel driverinvsel_9
  assign DATA_out = ~nBIT_DATout ? 8'h1 : 8'bz;  // DriverInvSel driverinvsel_10
  assign ADDRESS_LOout = ~RST_Vout ? 8'hf9 : 8'bz;  // DriverInvSel driverinvsel_11
  assign ADDRESS_LOout = ~NMI_Vout ? {8{1'b1}} : 8'bz;  // DriverInvSel driverinvsel_12
  assign ADDRESS_LOout = ~BRK_Vout ? {8{1'b1}} : 8'bz;  // DriverInvSel driverinvsel_13
  assign ADDRESS_LOout = ~IRJ_Vout ? {8{1'b1}} : 8'bz;  // DriverInvSel driverinvsel_14
  assign ADDRESS_LOout = ~IRK_Vout ? {8{1'b1}} : 8'bz;  // DriverInvSel driverinvsel_15
  PullDown pulldown_25 (.out(ADDRESS_LOin[5]));
  PullDown pulldown_26 (.out(ADDRESS_LOin[4]));
  PullDown pulldown_27 (.out(ADDRESS_LOin[3]));
  PullDown pulldown_28 (.out(ADDRESS_LOin[2]));
  PullDown pulldown_29 (.out(D5));
  PullDown pulldown_30 (.out(D4));
  PullDown pulldown_31 (.out(D3));
  PullDown pulldown_32 (.out(D2));
  assign ADDRESS_HIout = ~RST_Vout ? {8{1'b1}} : 8'bz;  // DriverInvSel driverinvsel_16
  PullDown #(.Bits(8)) pulldown_33 (.out(ADDRESS_HIout));
  assign ADDRESS_HIout = ~NMI_Vout ? 8'hf7 : 8'bz;  // DriverInvSel driverinvsel_17
  assign ADDRESS_HIout = ~BRK_Vout ? 8'hf5 : 8'bz;  // DriverInvSel driverinvsel_18
  assign ADDRESS_HIout = ~IRJ_Vout ? 8'hf3 : 8'bz;  // DriverInvSel driverinvsel_19
  assign ADDRESS_HIout = ~IRK_Vout ? 8'hf1 : 8'bz;  // DriverInvSel driverinvsel_20
  and and_20 (nPCH_st, not_57_out, not_58_out);
  and and_21 (nPCL_st, not_57_out, not_59_out);
  and and_22 (nIXH_st, not_61_out, not_62_out);
  and and_23 (nIXL_st, not_61_out, not_63_out);
  and and_24 (nIYH_st, not_64_out, not_65_out);
  and and_25 (nIYL_st, not_64_out, not_66_out);
  and and_26 (nMEM_en, nMEM_in, nMEM_DATout);
  PullDown pulldown_34 (.out(ADDRESS_LOin[1]));
  PullDown pulldown_35 (.out(ADDRESS_LOin[0]));
  PullDown pulldown_36 (.out(D1));
  PullDown pulldown_37 (.out(D0));
  PullDown #(.Bits(8)) pulldown_38 (.out(DATA_out));
  PullDown #(.Bits(8)) pulldown_39 (.out(DATA_out));
  PullDown #(.Bits(8)) pulldown_40 (.out(ADDRESS_LOout));
  or or_16 (or_16_out, CLK2, A_clr);
  assign driverinvsel_21_out = ~nREG_DATin ? {D7, D6, D5, D4, D3, D2, D1, D0} : 8'bz;  // DriverInvSel driverinvsel_21
  assign driverinvsel_22_out = ~nREG_ADDin ? ADDRESS_LOin : 8'bz;  // DriverInvSel driverinvsel_22
  PullDown #(.Bits(8)) pulldown_41 (.out(driverinvsel_22_out));
  assign driverinvsel_23_out = ~nREG_DATin ? {D7, D6, D5, D4, D3, D2, D1, D0} : 8'bz;  // DriverInvSel driverinvsel_23
  assign driverinvsel_24_out = ~nREG_ADDin ? ADDRESS_HIin : 8'bz;  // DriverInvSel driverinvsel_24
  CounterPreset #(.Bits(8)) A (
    .en(~1'b1), .C(or_16_out), .dir(1'b0), .in({D7, D6, D5, D4, D3, D2, D1, D0}), .ld(~nA_st), .clr(A_clr),
    .out(A_out));  // open: ovf
  assign or_17_out = driverinvsel_21_out | driverinvsel_22_out;  // Or or_17, 8 bits wide
  assign or_18_out = driverinvsel_23_out | driverinvsel_24_out;  // Or or_18, 8 bits wide
  PullDown #(.Bits(8)) pulldown_42 (.out(driverinvsel_24_out));
  Register #(.Bits(8)) MDR (.D({D7, D6, D5, D4, D3, D2, D1, D0}), .C(CLK2), .en(~nMDR_st), .Q(MDR_q));
  PullDown #(.Bits(8)) pulldown_43 (.out(or_17_out));
  PullDown #(.Bits(8)) pulldown_44 (.out(or_18_out));
  assign DATA_out = ~nA_DATout ? A_out : 8'bz;  // DriverInvSel driverinvsel_25
  PullDown #(.Bits(8)) pulldown_45 (.out(DATA_out));
  CounterPreset #(.Bits(8)) IYL (
    .en(~1'b1), .C(CLK2), .dir(1'b0), .in(or_17_out), .ld(~nIYL_st), .clr(IY_clr), .out(IYL_out));  // open: ovf
  CounterPreset #(.Bits(8)) IYH (
    .en(~1'b1), .C(CLK2), .dir(1'b0), .in(or_18_out), .ld(~nIYH_st), .clr(IY_clr), .out(IYH_out));  // open: ovf
  assign DATA_out = ~nSUM_DATout ? TSR_q : 8'bz;  // DriverInvSel driverinvsel_26
  PullDown #(.Bits(8)) pulldown_46 (.out(DATA_out));
  assign ADDRESS_LOout = ~nIY_ADSout ? IYL_out : 8'bz;  // DriverInvSel driverinvsel_27
  assign DATA_out = ~nIYL_DATout ? IYL_out : 8'bz;  // DriverInvSel driverinvsel_28
  assign ADDRESS_HIout = ~nIY_ADSout ? IYH_out : 8'bz;  // DriverInvSel driverinvsel_29
  assign DATA_out = ~nIXH_DATout ? IYH_out : 8'bz;  // DriverInvSel driverinvsel_30
  assign DATA_out = ~nMDR_DATout ? MDR_q : 8'bz;  // DriverInvSel driverinvsel_31
  PullDown #(.Bits(8)) pulldown_47 (.out(DATA_out));
  PullDown pulldown_48 (.out(Clock));
  PullDown #(.Bits(8)) pulldown_49 (.out(DATA_out));
  PullDown #(.Bits(8)) pulldown_50 (.out(ADDRESS_LOout));
  PullDown #(.Bits(8)) pulldown_51 (.out(DATA_out));
  PullDown #(.Bits(8)) pulldown_52 (.out(ADDRESS_HIout));
  Register #(.Bits(8)) TSR (.D(alu_1_p1), .C(CLK2), .en(~nSUM_st), .Q(TSR_q));
  T_FF #(.withEnable("false")) t_ff_1 (.C(not_82_out), .Q(t_ff_1_q), .nQ(t_ff_1_nq));
  not not_82 (not_82_out, Clock);
  PullDown #(.Bits(8)) pulldown_53 (.out(DATA_out));
  // ALU alu_1: pin names not known; wires that end beside it: alu_1_p1, \Σ_rot , \Σ_Csel , \Σ_Cval , A_out, FLAG_C, {D7, D6, D5, D4, D3, D2, D1, D0}, nF_ALUin, \Σ_M , \Σ_sel , alu_1_p11[0], alu_1_p11[1], alu_1_p13, alu_1_p14
  and and_27 (CLK1, Clock, t_ff_1_q);
  and and_28 (CLK2, t_ff_1_nq, ~nWAIT, Clock);  // And
  CounterPreset #(.Bits(8)) MARL (
    .en(~1'b1), .C(CLK2), .dir(1'b0), .in({D7, D6, D5, D4, D3, D2, D1, D0}), .ld(~nMARL_st), .clr(TEMP_clr),
    .out(MARL_out));  // open: ovf
  CounterPreset #(.Bits(8)) MARH (
    .en(~1'b1), .C(CLK2), .dir(1'b0), .in({D7, D6, D5, D4, D3, D2, D1, D0}), .ld(~nMARH_st), .clr(TEMP_clr),
    .out(MARH_out));  // open: ovf
  assign DATA_out = ~nF_DATout ? {IRK_FTdat, IRJ_FTdat, Y_FTdat, X_FTdat, FLAG_C, FLAG_V, FLAG_NZ} : 8'bz;  // DriverInvSel driverinvsel_32
  PullDown #(.Bits(2)) pulldown_54 (.out(alu_1_p11));
  Register #(.Bits(2)) NZ_F (.D(alu_1_p11), .C(CLK2), .en(~nNZ_Fst), .Q(FLAG_NZ));
  PullDown pulldown_55 (.out(alu_1_p14));
  PullDown pulldown_56 (.out(alu_1_p13));
  assign alu_1_p11 = ~nF_DATin ? {D1, D0} : 2'bz;  // DriverInvSel driverinvsel_33
  assign driverinvsel_34_out = ~nREG_ADDin ? ADDRESS_LOin : 8'bz;  // DriverInvSel driverinvsel_34
  assign driverinvsel_35_out = ~nREG_ADDin ? ADDRESS_HIin : 8'bz;  // DriverInvSel driverinvsel_35
  assign driverinvsel_36_out = ~nREG_DATin ? {D7, D6, D5, D4, D3, D2, D1, D0} : 8'bz;  // DriverInvSel driverinvsel_36
  assign or_19_out = driverinvsel_36_out | driverinvsel_34_out;  // Or or_19, 8 bits wide
  PullDown #(.Bits(8)) pulldown_57 (.out(driverinvsel_34_out));
  assign driverinvsel_37_out = ~nREG_DATin ? {D7, D6, D5, D4, D3, D2, D1, D0} : 8'bz;  // DriverInvSel driverinvsel_37
  assign or_20_out = driverinvsel_37_out | driverinvsel_35_out;  // Or or_20, 8 bits wide
  PullDown #(.Bits(8)) pulldown_58 (.out(driverinvsel_35_out));
  Register V_F (.D(alu_1_p14), .C(CLK2), .en(~nV_Fst), .Q(FLAG_V));
  assign alu_1_p14 = ~nF_DATin ? D2 : 1'bz;  // DriverInvSel driverinvsel_38
  PullDown #(.Bits(8)) pulldown_59 (.out(or_19_out));
  PullDown #(.Bits(8)) pulldown_60 (.out(or_20_out));
  assign ADDRESS_LOout = ~nMAR_ADSout ? MARL_out : 8'bz;  // DriverInvSel driverinvsel_39
  PullDown #(.Bits(8)) pulldown_61 (.out(ADDRESS_LOout));
  assign ADDRESS_HIout = ~nMAR_ADSout ? MARH_out : 8'bz;  // DriverInvSel driverinvsel_40
  PullDown #(.Bits(8)) pulldown_62 (.out(ADDRESS_HIout));
  Register nC_F (.D(alu_1_p13), .C(CLK2), .en(~nC_Fst), .Q(FLAG_C));
  assign alu_1_p13 = ~nF_DATin ? D3 : 1'bz;  // DriverInvSel driverinvsel_41
  CounterPreset #(.Bits(8)) IXL (
    .en(~1'b1), .C(CLK2), .dir(1'b0), .in(or_19_out), .ld(~nIXL_st), .clr(IX_clr), .out(IXL_out));  // open: ovf
  CounterPreset #(.Bits(8)) IXH (
    .en(~1'b1), .C(CLK2), .dir(1'b0), .in(or_20_out), .ld(~nIXH_st), .clr(IX_clr), .out(IXH_out));  // open: ovf
  assign DATA_out = ~nIXL_DATout ? IXL_out : 8'bz;  // DriverInvSel driverinvsel_42
  assign DATA_out = ~nIXH_DATout ? IXH_out : 8'bz;  // DriverInvSel driverinvsel_43
  assign ADDRESS_LOout = ~nIX_ADSout ? IXL_out : 8'bz;  // DriverInvSel driverinvsel_44
  PullDown #(.Bits(8)) pulldown_63 (.out(DATA_out));
  PullDown #(.Bits(8)) pulldown_64 (.out(ADDRESS_LOout));
  assign ADDRESS_HIout = ~nIX_ADSout ? IXH_out : 8'bz;  // DriverInvSel driverinvsel_45
  PullDown #(.Bits(8)) pulldown_65 (.out(DATA_out));
  PullDown #(.Bits(8)) pulldown_66 (.out(ADDRESS_HIout));
  assign driverinvsel_46_out = ~nREG_DATin ? {D7, D6, D5, D4, D3, D2, D1, D0} : 8'bz;  // DriverInvSel driverinvsel_46
  assign driverinvsel_47_out = ~nREG_ADDin ? ADDRESS_LOin : 8'bz;  // DriverInvSel driverinvsel_47
  assign driverinvsel_48_out = ~nREG_DATin ? {D7, D6, D5, D4, D3, D2, D1, D0} : 8'bz;  // DriverInvSel driverinvsel_48
  assign driverinvsel_49_out = ~nREG_ADDin ? ADDRESS_HIin : 8'bz;  // DriverInvSel driverinvsel_49
  assign or_21_out = driverinvsel_46_out | driverinvsel_47_out;  // Or or_21, 8 bits wide
  PullDown #(.Bits(8)) pulldown_67 (.out(driverinvsel_47_out));
  PullDown #(.Bits(8)) pulldown_68 (.out(driverinvsel_46_out));
  assign or_22_out = driverinvsel_48_out | driverinvsel_49_out;  // Or or_22, 8 bits wide
  PullDown #(.Bits(8)) pulldown_69 (.out(driverinvsel_49_out));
  PullDown #(.Bits(8)) pulldown_70 (.out(driverinvsel_48_out));
  PullDown #(.Bits(8)) pulldown_71 (.out(or_21_out));
  PullDown #(.Bits(8)) pulldown_72 (.out(or_22_out));
  LED u_D6 (.in(D6));
  LED u_D7 (.in(D7));
  LED A14 (.in(ADDRESS_HIin[6]));
  LED A15 (.in(ADDRESS_HIin[7]));
  not not_83 (not_83_out, PCL_ovf);
  LED u_D5 (.in(D5));
  LED A13 (.in(ADDRESS_HIin[5]));
  CounterPreset #(.Bits(8)) PCL (
    .en(~PC_en), .C(CLK2), .dir(pcd), .in(or_21_out), .ld(~nPCL_st), .clr(1'b0), .out(PCL_out), .ovf(PCL_ovf));
  CounterPreset #(.Bits(8)) PCH (
    .en(~not_83_out), .C(CLK2), .dir(pcd), .in(or_22_out), .ld(~nPCH_st), .clr(1'b0), .out(PCH_out));  // open: ovf
  or or_23 (or_23_out, CLK2, BCD_clr);
  or or_24 (or_24_out, CLK2, BCD_clr);
  or or_25 (or_25_out, CLK2, BCD_clr);
  LED u_D4 (.in(D4));
  LED A12 (.in(ADDRESS_HIin[4]));
  CounterPreset #(.Bits(8)) REL (
    .en(~1'b1), .C(CLK2), .dir(1'b0), .in({D7, D6, D5, D4, D3, D2, D1, D0}), .ld(~nREL_st), .clr(TEMP_clr),
    .out(REL_out));  // open: ovf
  LED u_D2 (.in(D2));
  LED u_D3 (.in(D3));
  LED A10 (.in(ADDRESS_HIin[2]));
  LED A11 (.in(ADDRESS_HIin[3]));
  CounterPreset #(.Bits(8)) B (
    .en(~1'b1), .C(or_23_out), .dir(1'b0), .in({D7, D6, D5, D4, D3, D2, D1, D0}), .ld(~nB_st), .clr(BCD_clr),
    .out(B_out));  // open: ovf
  CounterPreset #(.Bits(8)) C (
    .en(~1'b1), .C(or_24_out), .dir(1'b0), .in({D7, D6, D5, D4, D3, D2, D1, D0}), .ld(~nC_st), .clr(BCD_clr),
    .out(C_out));  // open: ovf
  CounterPreset #(.Bits(8)) D (
    .en(~1'b1), .C(or_25_out), .dir(1'b0), .in({D7, D6, D5, D4, D3, D2, D1, D0}), .ld(~nD_st), .clr(BCD_clr),
    .out(D_out));  // open: ovf
  CounterPreset #(.Bits(8)) SP (
    .en(~SP_en), .C(CLK2), .dir(SP_dir), .in({D7, D6, D5, D4, D3, D2, D1, D0}), .ld(~nSP_st), .clr(1'b0),
    .out(SP_out));  // open: ovf
  LED u_D1 (.in(D1));
  LED A9 (.in(ADDRESS_HIin[1]));
  CounterPreset #(.Bits(8)) ADDL (
    .en(~1'b1), .C(CLK2), .dir(1'b0), .in(ADDRESS_LOin), .ld(~nTADD_st), .clr(TEMP_clr), .out(ADDL_out));  // open: ovf
  BitExtender #(.inputBits(7), .outputBits(8)) bitextender_1 (.in(REL_out[6:0]), .out(bitextender_1_out));
  BitExtender #(.inputBits(1), .outputBits(8)) bitextender_2 (.in(REL_out[7]), .out(bitextender_2_out));
  CounterPreset #(.Bits(8)) ADDH (
    .en(~1'b1), .C(CLK2), .dir(1'b0), .in(ADDRESS_HIin), .ld(~nTADD_st), .clr(TEMP_clr), .out(ADDH_out));  // open: ovf
  assign ADDRESS_LOout = ~nBC_ADSout ? B_out : 8'bz;  // DriverInvSel driverinvsel_50
  assign ADDRESS_HIout = ~nBC_ADSout ? C_out : 8'bz;  // DriverInvSel driverinvsel_51
  assign DATA_out = ~nD_DATout ? D_out : 8'bz;  // DriverInvSel driverinvsel_52
  LED u_D0 (.in(D0));
  LED A8 (.in(ADDRESS_HIin[0]));
  assign DATA_out = ~nB_DATout ? B_out : 8'bz;  // DriverInvSel driverinvsel_53
  assign DATA_out = ~nC_DATout ? C_out : 8'bz;  // DriverInvSel driverinvsel_54
  LED A6 (.in(ADDRESS_LOin[6]));
  LED A7 (.in(ADDRESS_LOin[7]));
  Add #(.Bits(8)) add_1 (.a(ADDL_out), .b(bitextender_1_out), .c_i(1'b0), .s(add_1_s), .c_o(add_1_c_o));
  Add #(.Bits(8)) add_2 (.a(ADDH_out), .b(bitextender_2_out), .c_i(add_1_c_o), .s(add_2_s));  // open: c_o
  assign ADDRESS_LOout = ~nSP_ADSout ? SP_out : 8'bz;  // DriverInvSel driverinvsel_55
  assign DATA_out = ~nSP_DATout ? SP_out : 8'bz;  // DriverInvSel driverinvsel_56
  LED Y (.in(Y_FTdat));
  LED A5 (.in(ADDRESS_LOin[5]));
  assign ADDRESS_LOout = ~nADD_ADSout ? add_1_s : 8'bz;  // DriverInvSel driverinvsel_57
  assign ADDRESS_LOout = ~nPC_ADSout ? PCL_out : 8'bz;  // DriverInvSel driverinvsel_58
  assign DATA_out = ~nPCL_DATout ? PCL_out : 8'bz;  // DriverInvSel driverinvsel_59
  assign ADDRESS_HIout = ~nPC_ADSout ? PCH_out : 8'bz;  // DriverInvSel driverinvsel_60
  assign DATA_out = ~nPCH_DATout ? PCH_out : 8'bz;  // DriverInvSel driverinvsel_61
  PullDown #(.Bits(8)) pulldown_73 (.out(DATA_out));
  PullDown #(.Bits(8)) pulldown_74 (.out(ADDRESS_LOout));
  PullDown #(.Bits(8)) pulldown_75 (.out(DATA_out));
  PullDown #(.Bits(8)) pulldown_76 (.out(ADDRESS_HIout));
  PullDown #(.Bits(8)) pulldown_77 (.out(DATA_out));
  assign ADDRESS_HIout = ~nSP_ADSout ? 8'h1 : 8'bz;  // DriverInvSel driverinvsel_62
  PullDown #(.Bits(8)) pulldown_78 (.out(ADDRESS_HIout));
  PullDown #(.Bits(8)) pulldown_79 (.out(ADDRESS_LOout));
  PullDown #(.Bits(8)) pulldown_80 (.out(DATA_out));
  LED X (.in(X_FTdat));
  LED A4 (.in(ADDRESS_LOin[4]));
  PullDown #(.Bits(8)) pulldown_81 (.out(ADDRESS_LOout));
  assign ADDRESS_HIout = ~nADD_ADSout ? add_2_s : 8'bz;  // DriverInvSel driverinvsel_63
  PullDown #(.Bits(8)) pulldown_82 (.out(ADDRESS_HIout));
  PullDown #(.Bits(8)) pulldown_83 (.out(DATA_out));
  PullDown #(.Bits(8)) pulldown_84 (.out(ADDRESS_LOout));
  PullDown #(.Bits(8)) pulldown_85 (.out(DATA_out));
  PullDown #(.Bits(8)) pulldown_86 (.out(ADDRESS_HIout));
  LED V (.in(FLAG_V));
  LED C_2 (.in(not_84_out));
  not not_84 (not_84_out, FLAG_C);
  LED A2 (.in(ADDRESS_LOin[2]));
  LED A3 (.in(ADDRESS_LOin[3]));
  LED Z (.in(FLAG_NZ[1]));
  LED A1 (.in(ADDRESS_LOin[1]));
  LED N (.in(FLAG_NZ[0]));
  LED A0 (.in(ADDRESS_LOin[0]));

  // Other names for the same wires on the sheet: CLK_1 = CLK1; CLK_2 = CLK2;
  //   DATA_in[7:0] = {D7, D6, D5, D4, D3, D2, D1, D0}; nMEM_st = nMEM_in

  // Notes on the sheet:
  //   Clock: Hz: 10
  //   nRST: default 1
  //   nNMI: default 1
  //   nIRJ: default 1
  //   nIRK: default 1
  //   nDMA: default 1
  //   nHALT: default 1
  //   Control Sequencing
  //   Conditionals/Misc Control
  //   MEM/BUS
  //   contents of rom_1 (hex, n*v repeats v):
  //   0,0,0,0,0,0,0,0,0,0,0,0,0,0,0,0,0,0,0,0,0,0,0,0,0,0,0,0,0,0,0,0,0,0,0,0,0,0,0,0,0,
  //   0,0,0,0,0,0,0,0,0,0,0,0,0,0,0,0,0,0,0,0,0,0,0,0,0,0,0,0,0,0,0,0,0,0,0,0,0,0,0,0,0,
  //   0,0,0,0,0,0,0,0,0,0,0,0,0,0,0,0,0,0,0,0,0,0,0,0,0,0,0,0,0,0,0,0,0,0,0,0,0,0,0,0,0,
  //   0,0,0,0,0,0,0,0,0,0,0,0,0,0,0,0,0,0,0,0,0,0,0,0,0,0,0,0,0,0,0,0,0,0,0,0,0,0,0,0,0,
  //   0,0,0,0,0,0,0,0,0,0,0,0,0,0,0,0,0,0,0,0,0,0,0,0,0,0,0,0,0,0,0,0,0,0,0,0,0,0,0,0,0,
  //   0,0,0,0,0,0,0,0,0,0,0,0,0,0,0,0,0,0,0,0,0,0,0,0,0,0,0,0,0,0,0,0,0,0,0,0,0,0,0,0,0,
  //   0,0,0,0,0,0,0,0,0,0,0,0,0,0,0,0,0,0,0,0,0,0,0,0,0,0,0,0,0,0,0,0,0,0,0,0,0,0,0,0,0,
  //   0,0,0,0,0,0,0,0,0,0,0,0,0,0,0,0,0,0,0,0,0,0,0,0,0,0,0,0,0,0,0,0,0,0,0,0,0,0,0,0,0,
  //   0,0,0,0,0,0,0,0,0,0,0,0,0,0,0,0,0,0,0,0,0,0,0,0,0,0,0,0,0,0,0,0,0,0,0,0,0,0,0,0,0,
  //   0,0,0,0,0,0,0,0,0,0,0,0,0,0,0,0,0,0,0,0,0,0,0,0,0,0,0,0,0,0,0,0,0,0,0,0,0,0,0,0,0,
  //   0,0,0,0,0,0,0,0,0,0,0,0,0,0,0,0,0,0,0,0,0,0,0,0,0,0,0,0,0,0,0,0,0,0,0,0,0,0,0,0,0,
  //   0,0,0,0,0,0,0,0,0,0,0,0,0,0,0,0,0,0,0,0,0,0,0,0,0,0,0,0,0,0,0,0,0,0,0,0,0,0,0,0,0,
  //   0,0,0,0,0,0,0,0,0,0,0,0,0,0,0,0,0,0,0,0,0,0,0,0,0,0,0,0,0,0,0,0,0,0,0,0,0,0,0,0,0,
  //   0,0,0,0,0,0,0,0,0,0,0,0,0,0,0,0,0,0,0,0,0,0,0,0,0,0,0,0,0,0,0,0,0,0,0,0,0,0,0,0,0,
  //   0,0,0,0,0,0,0,0,0,0,0,0,0,0,0,0,0,0,0,0,0,0,0,0,0,0,0,0,0,0,0,0,0,0,0,0,0,0,0,0,0,
  //   0,0,0,0,0,0,0,0,0,0,0,0,0,0,0,0,0,0,0,0,0,0,0,0,0,0,0,0,0,0,0,0,0,0,0,0,0,0,0,0,0,
  //   0,0,0,0,0,0,0,0,0,0,0,0,0,0,0,0,0,0,0,0,0,0,0,0,0,0,0,0,0,0,0,0,0,0,0,0,0,0,0,0,0,
  //   0,0,0,0,0,0,0,0,0,0,0,0,0,0,0,0,0,0,0,0,0,0,0,0,0,0,0,0,0,0,0,0,0,0,0,0,0,0,0,0,0,
  //   0,0,0,0,0,0,0,0,0,0,0,0,0,0,0,0,0,0,0,0,0,0,0,0,0,0,0,0,0,0,0,0,0,0,0,0,0,0,0,0,0,
  //   0,0,0,0,0,0,0,0,0,0,0,0,0,0,0,0,0,0,0,0,0,0,0,0,0,0,0,0,0,0,0,0,0,0,0,0,0,0,0,0,0,
  //   0,0,0,0,0,0,0,0,0,0,0,0,0,0,0,0,0,0,0,0,0,0,0,0,0,0,0,0,0,0,0,0,0,0,0,0,0,0,0,0,0,
  //   0,0,0,0,0,0,0,0,0,0,0,0,0,0,0,0,0,0,0,0,0,0,0,0,0,0,0,0,0,0,0,0,0,0,0,0,0,0,0,0,0,
  //   0,0,0,0,0,0,0,0,0,0,0,0,0,0,0,0,0,0,0,0,0,0,0,0,0,0,0,0,0,0,0,0,0,0,0,0,0,0,0,0,0,
  //   0,0,0,0,0,0,0,0,0,0,0,0,0,0,0,0,0,0,0,0,0,0,0,0,0,0,0,0,0,0,0,0,0,0,0,0,0,0,0,0,0,
  //   0,0,0,0,0,0,0,0,0,0,0,0,0,0,0,0,0,0,0,0,0,0,0,0,0,0,0,0,0,0,0,0,0,0,0,0,0,0,0,0,0,
  //   0,0,0,0,0,0,0,0,0,0,0,0,0,0,0,0,0,0,0,0,0,0,0,0,0,0,0,0,0,0,0,0,0,0,0,0,0,0,0,0,0,
  //   0,0,0,0,0,0,0,0,0,0,0,0,0,0,0,0,0,0,0,0,0,0,0,0,0,0,0,0,0,0,0,0,0,0,0,0,0,0,0,0,0,
  //   0,0,0,0,0,0,0,0,0,0,0,0,0,0,0,0,0,0,0,0,0,0,0,0,0,0,0,0,0,0,0,0,0,0,0,0,0,0,0,0,0,
  //   0,0,0,0,0,0,0,0,0,0,0,0,0,0,0,0,0,0,0,0,0,0,0,0,0,0,0,0,0,0,0,0,0,0,0,0,0,0,0,0,0,
  //   0,0,0,0,0,0,0,0,0,0,0,0,0,0,0,0,0,0,0,0,0,0,0,0,0,0,0,0,0,0,0,0,0,0,0,0,0,0,0,0,0,
  //   0,0,0,0,0,0,0,0,0,0,0,0,0,0,0,0,0,0,0,0,0,0,0,0,0,0,0,0,0,0,0,0,0,0,0,0,0,0,0,0,0,
  //   0,0,0,0,0,0,0,0,0,0,0,0,0,0,0,0,0,0,0,0,0,0,0,0,0,0,0,0,0,0,0,0,0,0,0,0,0,0,0,0,0,
  //   0,0,0,0,0,0,0,0,0,0,0,0,0,0,0,0,0,0,0,0,0,0,0,0,0,0,0,0,0,0,0,0,0,0,0,0,0,0,0,0,0,
  //   0,0,0,0,0,0,0,0,0,0,0,0,0,0,0,0,0,0,0,0,0,0,0,0,0,0,0,0,0,0,0,0,0,0,0,0,0,0,0,0,0,
  //   0,0,0,0,0,0,0,0,0,0,0,0,0,0,0,0,0,0,0,0,0,0,0,0,0,0,0,0,0,0,0,0,0,0,0,0,0,0,0,0,0,
  //   0,0,0,0,0,0,0,0,0,0,0,0,0,0,0,0,0,0,0,0,0,0,0,0,0,0,0,0,0,0,0,0,0,0,0,0,0,0,0,0,0,
  //   0,0,0,0,0,0,0,0,0,0,0,0,0,0,0,0,0,0,0,0,0,0,0,0,0,0,0,0,0,0,0,0,0,0,0,0,0,0,0,0,0,
  //   0,0,0,0,0,0,0,0,0,0,0,0,0,0,0,0,0,0,0,0,0,0,0,0,0,0,0,0,0,0,0,0,0,0,0,0,0,0,0,0,0,
  //   0,0,0,0,0,0,0,0,0,0,0,0,0,0,0,0,0,0,0,0,0,0,0,0,0,0,0,0,0,0,0,0,0,0,0,0,0,0,0,0,0,
  //   0,0,0,0,0,0,0,0,0,0,0,0,0,0,0,0,0,0,0,0,0,0,0,0,0,0,0,0,0,0,0,0,0,0,0,0,0,0,0,0,0,
  //   0,0,0,0,0,0,0,0,0,0,0,0,0,0,0,0,0,0,0,0,0,0,0,0,0,0,0,0,0,0,0,0,0,0,0,0,0,0,0,0,0,
  //   0,0,0,0,0,0,0,0,0,0,0,0,0,0,0,0,0,0,0,0,0,0,0,0,0,0,0,0,0,0,0,0,0,0,0,0,0,0,0,0,0,
  //   0,0,0,0,0,0,0,0,0,0,0,0,0,0,0,0,0,0,0,0,0,0,0,0,0,0,0,0,0,0,0,0,0,0,0,0,0,0,0,0,0,
  //   0,0,0,0,0,0,0,0,0,0,0,0,0,0,0,0,0,0,0,0,0,0,0,0,0,0,0,0,0,0,0,0,0,0,0,0,0,0,0,0,0,
  //   0,0,0,0,0,0,0,0,0,0,0,0,0,0,0,0,0,0,0,0,0,0,0,0,0,0,0,0,0,0,0,0,0,0,0,0,0,0,0,0,0,
  //   0,0,0,0,0,0,0,0,0,0,0,0,0,0,0,0,0,0,0,0,0,0,0,0,0,0,0,0,0,0,0,0,0,0,0,0,0,0,0,0,0,
  //   0,0,0,0,0,0,0,0,0,0,0,0,0,0,0,0,0,0,0,0,0,0,0,0,0,0,0,0,0,0,0,0,0,0,0,0,0,0,0,0,0,
  //   0,0,0,0,0,0,0,0,0,0,0,0,0,0,0,0,0,0,0,0,0,0,0,0,0,0,0,0,0,0,0,0,0,0,0,0,0,0,0,0,0,
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  //   contents of µCODE (hex, n*v repeats v):
  //   9000380254c,140020005cd,10000002560,12000440590,11000002561,241242c600d,0,0,0,0,0,
  //   0,0,0,0,0,0,0,0,0,0,0,0,0,0,0,0,0,0,0,0,0,180000000000,180000000000,180000000000,
  //   180000000000,180000000000,180000000000,180000000000,180000000000,180000000000,180000000000,
  //   180000000000,180000000000,180000000000,180000000000,180000000000,180000000000,180000000000,
  //   180000000000,180000000000,180000000000,180000000000,180000000000,180000000000,180000000000,
  //   180000000000,180000000000,180000000000,180000000000,180000000000,180000000000,180000000000,
  //   180000000000,9000380254c,140020005cd,10000002560,12000440590,11000002561,241242c600d,
  //   0,0,0,0,0,0,0,0,0,0,0,0,0,0,0,0,0,0,0,0,0,0,0,0,0,0,180000000000,180000000000,180000000000,
  //   180000000000,180000000000,180000000000,180000000000,180000000000,180000000000,180000000000,
  //   180000000000,180000000000,180000000000,180000000000,180000000000,180000000000,180000000000,
  //   180000000000,180000000000,180000000000,180000000000,180000000000,180000000000,180000000000,
  //   180000000000,180000000000,180000000000,180000000000,180000000000,180000000000,180000000000,
  //   180000000000,9000380254c,140020005cd,10000002560,12000440590,11000002561,241242c600d,
  //   0,0,0,0,0,0,0,0,0,0,0,0,0,0,0,0,0,0,0,0,0,0,0,0,0,0,180000000000,180000000000,180000000000,
  //   180000000000,180000000000,180000000000,180000000000,180000000000,180000000000,180000000000,
  //   180000000000,180000000000,180000000000,180000000000,180000000000,180000000000,180000000000,
  //   180000000000,180000000000,180000000000,180000000000,180000000000,180000000000,180000000000,
  //   180000000000,180000000000,180000000000,180000000000,180000000000,180000000000,180000000000,
  //   180000000000,9000380254c,140020005cd,10000002560,12000440590,11000002561,241242c600d,
  //   0,0,0,0,0,0,0,0,0,0,0,0,0,0,0,0,0,0,0,0,0,0,0,0,0,0,180000000000,180000000000,180000000000,
  //   180000000000,180000000000,180000000000,180000000000,180000000000,180000000000,180000000000,
  //   180000000000,180000000000,180000000000,180000000000,180000000000,180000000000,180000000000,
  //   180000000000,180000000000,180000000000,180000000000,180000000000,180000000000,180000000000,
  //   180000000000,180000000000,180000000000,180000000000,180000000000,180000000000,180000000000,
  //   180000000000,9000380254c,140020005cd,10000002560,12000440590,11000002561,241242c600d,
  //   0,0,0,0,0,0,0,0,0,0,0,0,0,0,0,0,0,0,0,0,0,0,0,0,0,0,180000000000,180000000000,180000000000,
  //   180000000000,180000000000,180000000000,180000000000,180000000000,180000000000,180000000000,
  //   180000000000,180000000000,180000000000,180000000000,180000000000,180000000000,180000000000,
  //   180000000000,180000000000,180000000000,180000000000,180000000000,180000000000,180000000000,
  //   180000000000,180000000000,180000000000,180000000000,180000000000,180000000000,180000000000,
  //   180000000000,9000380254c,140020005cd,10000002560,12000440590,11000002561,241242c600d,
  //   0,0,0,0,0,0,0,0,0,0,0,0,0,0,0,0,0,0,0,0,0,0,0,0,0,0,180000000000,180000000000,180000000000,
  //   180000000000,180000000000,180000000000,180000000000,180000000000,180000000000,180000000000,
  //   180000000000,180000000000,180000000000,180000000000,180000000000,180000000000,180000000000,
  //   180000000000,180000000000,180000000000,180000000000,180000000000,180000000000,180000000000,
  //   180000000000,180000000000,180000000000,180000000000,180000000000,180000000000,180000000000,
  //   180000000000,9000380254c,140020005cd,10000002560,12000440590,11000002561,241242c600d,
  //   0,0,0,0,0,0,0,0,0,0,0,0,0,0,0,0,0,0,0,0,0,0,0,0,0,0,180000000000,180000000000,180000000000,
  //   180000000000,180000000000,180000000000,180000000000,180000000000,180000000000,180000000000,
  //   180000000000,180000000000,180000000000,180000000000,180000000000,180000000000,180000000000,
  //   180000000000,180000000000,180000000000,180000000000,180000000000,180000000000,180000000000,
  //   180000000000,180000000000,180000000000,180000000000,180000000000,180000000000,180000000000,
  //   180000000000,9000380254c,140020005cd,10000002560,12000440590,11000002561,241242c600d,
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  //   ALU/PC
  //   ALU
  //   FRONT PANEL
  //   ATLAS CPU-8
  //   By Hayden B.
endmodule
